# Fritzing sketch Q1060-PCB Alimentação (saved by Fritzing 0.9.10b)
circuit board: 3.7cm x 2.2cm
breadboards: 1

parts:
  B = female pin header, 2 pins [form="♀ (female)"]
  C = female pin header, 2 pins [form="♀ (female)"]
  D = female pin header, 2 pins [form="♀ (female)"]
  5V = female pin header, 2 pins [form="♀ (female)"]
  BAT = female pin header, 2 pins [form="♀ (female)"]
  CAR = female pin header, 2 pins [form="♀ (female)"]
  CHV = female pin header, 2 pins [form="♀ (female)"]
  PTH = female pin header, 2 pins [form="♀ (female)"]
  VIN = female pin header, 2 pins [form="♀ (female)"]
  A = female pin header, 2 pins [form="♀ (female)"]

nets:
  N1: B.pin1, C.pin1, D.pin1, 5V.pin1, A.pin1
  N2: B.pin2, C.pin2, D.pin2, 5V.pin2, A.pin2
  N3: BAT.pin1, CAR.pin1, PTH.pin1, VIN.pin1
  N4: BAT.pin2, CAR.pin2, CHV.pin2
  N5: CHV.pin1, PTH.pin2, VIN.pin2
