# Fritzing sketch Q1060-Shield Arduino (1) (saved by Fritzing 0.9.10b)
circuit board: 4cm x 5.3cm

parts:
  Componente1 = Arduino Uno (Rev3)  # not connected
  Portas_0-7 = female pin header, 8 pins [form="♀ (female)"]
  PFonte = female pin header, 8 pins [form="♀ (female)"]
  PAnalogicas = female pin header, 6 pins [form="♀ (female)"]  # not connected
  J5 = female pin header, 4 pins [form="♀ (female)"]
  J8 = female pin header, 2 pins [form="♀ (female)"]
  J9 = female pin header, 4 pins [form="♀ (female)"]
  J6 = female pin header, 4 pins [form="♀ (female)"]
  Portas_8-13 = female pin header, 6 pins [form="♀ (female)"]
  J11 = female pin header, 2 pins [form="♀ (female)"]
  J10 = female pin header, 8 pins [form="♀ (female)"]

nets:
  N1: Portas_0-7.pin1, J9.pin1
  N2: Portas_0-7.pin2, J9.pin2
  N3: Portas_0-7.pin3, J9.pin3
  N4: Portas_0-7.pin4, J9.pin4
  N5: Portas_0-7.pin5, J8.pin1
  N6: Portas_0-7.pin6, J8.pin2
  N7: PFonte.pin5, J5.pin4
  N8: PFonte.pin6, J5.pin3
  N9: PFonte.pin7, J5.pin2
  N10: PFonte.pin8, J5.pin1
  N11: J6.pin1, Portas_8-13.pin3
  N12: J6.pin2, Portas_8-13.pin4
  N13: J6.pin3, Portas_8-13.pin5
  N14: J6.pin4, Portas_8-13.pin6
  N15: J11.pin2, J10.pin6
